// Logisim project WITCPU.circ as structural Verilog: 1 circuit, main circuit main
module main (
);

  wire clock_1_out, Rx_p2;
  wire [15:0] Rd_q, register_1_q, Rx_p3;
  wire [15:1] undriven;

  Clock clock_1 (.out(clock_1_out));
  Register #(.width(16)) Rd (.Q(Rd_q));  // open: D, en, clk, clr
  Register #(.width(16)) register_1 (.en(clock_1_out), .Q(register_1_q), .clr(Rd_q[0]));  // open: D, clk
  Register #(.width(16)) register_2 (.en(Rd_q[0]), .Q(register_1_q), .clr(Rd_q[0]));  // open: D, clk
  Register #(.width(16)) register_3 (.en(Rd_q[0]), .Q(register_1_q), .clr(Rd_q[0]));  // open: D, clk
  Register #(.width(16)) register_4 (.en(Rd_q[0]), .Q(register_1_q), .clr(Rd_q[0]));  // open: D, clk
  Register #(.width(16)) register_5 (.en(Rd_q[0]), .Q(register_1_q), .clr(Rd_q[0]));  // open: D, clk
  Register #(.width(16)) register_6 (.en(Rd_q[0]), .Q(register_1_q), .clr(Rd_q[0]));  // open: D, clk
  Register #(.width(16)) register_7 (.en(Rd_q[0]), .Q(register_1_q), .clr(Rd_q[0]));  // open: D, clk
  Register #(.width(16)) register_8 (.en(Rd_q[0]), .Q(register_1_q), .clr(Rd_q[0]));  // open: D, clk
  Register #(.width(16)) register_9 (.en(Rd_q[0]), .Q(register_1_q), .clr(register_1_q[0]));  // open: D, clk
  Register #(.width(16)) register_10 (.en(Rd_q[0]), .Q(register_1_q), .clr(register_1_q[0]));  // open: D, clk
  Register #(.width(16)) register_11 (.en(Rd_q[0]), .Q(register_1_q), .clr(register_1_q[0]));  // open: D, clk
  Register #(.width(16)) register_12 (.en(Rd_q[0]), .Q(register_1_q), .clr(register_1_q[0]));  // open: D, clk
  Register #(.width(16)) register_13 (.en(Rd_q[0]), .Q(register_1_q), .clr(register_1_q[0]));  // open: D, clk
  Register #(.width(16)) register_14 (.en(Rd_q[0]), .Q(register_1_q), .clr(register_1_q[0]));  // open: D, clk
  Register #(.width(16)) register_15 (.en(Rd_q[0]), .Q(register_1_q), .clr(register_1_q[0]));  // open: D, clk
  Register #(.width(16)) register_16 (.en(Rd_q[0]), .Q(register_1_q), .clr(register_1_q[0]));  // open: D, clk
  // Register #(.width(16)) Rx: pin names not known; wires that end beside it: register_1_q[0], Rx_p2, Rx_p3
  Register #(.width(16)) Ry (.D({undriven, register_1_q[1]}), .Q(Rx_p3));  // open: en, clk, clr
  // Pins of 1 and 16 bits meet at Rd_q
  // Pins of 1 and 2 and 16 bits meet at register_1_q
  // Pins of 1 and 16 bits meet at {undriven, register_1_q[1]}

  // Notes on the sheet:
  //   R0
  //   R1
  //   R2
  //   R3
  //   R4
  //   R5
  //   R6
  //   R7
  //   R8
  //   R9
  //   Ra
  //   Rb
  //   Rc
  //   Rd
  //   Re
  //   Rf
endmodule
